// Logisim project myCirciut.circ as structural Verilog: 1 circuit, main circuit main
module main (
  input  x,
  input  y,
  output [3:0] z
);

  wire and_2_out, clock_1_out, d_ff_1_q, not_1_out, not_2_out;

  Clock clock_1 (.out(clock_1_out));
  D_Flip_Flop d_ff_1 (.clk(clock_1_out), .D(x), .Q(d_ff_1_q));  // open: Qn, preset, en, reset
  not not_1 (not_1_out, d_ff_1_q);
  D_Flip_Flop d_ff_2 (.clk(clock_1_out), .D(y), .Q(z[0]));  // open: Qn, preset, en, reset
  and and_1 (z[3], d_ff_1_q, z[0]);
  and and_2 (and_2_out, not_1_out, z[0]);
  and and_3 (z[2], d_ff_1_q, not_2_out);
  not not_2 (not_2_out, z[0]);
  or or_1 (z[1], and_2_out, z[2]);

  // Notes on the sheet:
  //   n1
  //   s1
  //   n0
  //   s0
  //   s1s0
  //   s1's0
  //   s1s0'
  //   a
  //   b
  //   c
  //   d
endmodule
