// Logisim project myCirc.circ as structural Verilog: 1 circuit, main circuit main
module main (
  input  x,
  input  reset,
  output out_3
);

  wire clock_1_out, not_1_out, not_2_out, or_1_out, or_2_out, or_3_out, or_4_out, or_5_out;
  wire [6:0] d_ff_1_q, register_1_q;

  D_Flip_Flop d_ff_1 (.clk(clock_1_out), .D(reset), .Q(d_ff_1_q[0]));  // open: Qn, preset, en, reset
  Clock clock_1 (.out(clock_1_out));
  not not_1 (not_1_out, x);
  not not_2 (not_2_out, d_ff_1_q[0]);
  Register #(.width(7)) register_1 (.D(d_ff_1_q), .en(1'b1), .Q(register_1_q), .clk(clock_1_out));  // open: clr
  or or_1 (or_1_out, register_1_q[6], register_1_q[5], register_1_q[4], register_1_q[0]);
  or or_2 (or_2_out, register_1_q[3], register_1_q[2]);
  or or_3 (or_3_out, register_1_q[0], register_1_q[1], register_1_q[2], register_1_q[3]);
  or or_4 (or_4_out, register_1_q[6], register_1_q[5]);
  or or_5 (or_5_out, register_1_q[6], register_1_q[3]);
  and and_1 (d_ff_1_q[1], x, not_2_out, or_1_out);
  and and_2 (d_ff_1_q[2], not_2_out, x, register_1_q[1]);
  and and_3 (d_ff_1_q[3], not_2_out, x, or_2_out);
  and and_4 (d_ff_1_q[4], not_1_out, not_2_out, or_3_out);
  and and_5 (d_ff_1_q[5], not_2_out, not_1_out, register_1_q[4]);
  and and_6 (d_ff_1_q[6], not_2_out, not_1_out, or_4_out);
  and and_7 (out_3, not_2_out, or_5_out);

  // Notes on the sheet:
  //   s
  //   n
endmodule
