// Logisim project circpre6.circ as structural Verilog: 1 circuit, main circuit main
module main (
  input  start,
  input  up_max,
  input  index_lt_eight,
  output max_clr,
  output index_clr,
  output max_index_clr,
  output completed_ld,
  output completed_clr,
  output index_ld,
  output max_ld,
  output max_index_ld
);

  wire and_1_out, and_3_out, and_4_out, and_5_out, and_6_out, and_7_out, clock_1_out, not_1_out, not_2_out,
       not_3_out, not_4_out, not_5_out;
  wire [2:0] or_2_out, register_1_q;

  not not_1 (not_1_out, index_lt_eight);
  not not_2 (not_2_out, register_1_q[2]);
  Clock clock_1 (.out(clock_1_out));
  not not_3 (not_3_out, up_max);
  not not_4 (not_4_out, register_1_q[0]);
  not not_5 (not_5_out, register_1_q[1]);
  Register #(.width(3)) register_1 (.D(or_2_out), .en(1'b1), .Q(register_1_q), .clk(clock_1_out));  // open: clr
  and and_1 (and_1_out, not_3_out, not_2_out, register_1_q[1], not_4_out);
  and and_2 (max_index_ld, not_2_out, register_1_q[1], register_1_q[0]);
  and and_3 (and_3_out, register_1_q[2], not_5_out, not_4_out, not_1_out);
  and and_4 (and_4_out, not_2_out, not_5_out, register_1_q[0]);
  and and_5 (and_5_out, not_2_out, register_1_q[1], not_4_out, up_max);
  and and_6 (and_6_out, register_1_q[2], not_5_out, not_4_out, index_lt_eight);
  and and_7 (and_7_out, not_2_out, not_5_out, not_4_out, start);
  and and_8 (completed_clr, not_2_out, not_5_out, not_4_out);
  and and_9 (completed_ld, register_1_q[2], not_5_out, register_1_q[0]);
  and and_10 (index_ld, register_1_q[2], not_5_out, not_4_out);
  or or_1 (or_2_out[1], and_4_out, and_5_out, and_6_out);
  or or_2 (or_2_out[0], and_3_out, and_5_out, and_7_out);
  or or_3 (or_2_out[2], and_1_out, max_index_ld, and_3_out);

  assign index_clr = completed_clr;
  assign max_clr = completed_clr;
  assign max_index_clr = completed_clr;
  assign max_ld = max_index_ld;

  // Notes on the sheet:
  //   s
  //   n
endmodule
